# Fritzing sketch 40106 ORDERED (saved by Fritzing 0.9.1b)
circuit board: 4.88393cm x 5.13644cm
breadboards: 1

parts:
  darcyneal_com = Optocoupler [package=THT]
  R11 = Resistor [tolerance=±5% resistance=10k package=THT]
  R10 = Resistor [tolerance=±5% resistance=10k package=THT]
  R12 = Resistor [tolerance=±5% resistance=10k package=THT]
  C10 = Electrolytic Capacitor [capacitance=1µF package="100 mil [THT, electrolytic]"]
  C9 = Electrolytic Capacitor [capacitance=1µF package="100 mil [THT, electrolytic]"]
  R13 = Resistor [tolerance=±5% resistance=2.2k package=THT]
  R9 = Resistor [tolerance=±5% resistance=220 package=THT]
  R8 = Resistor [tolerance=±5% resistance=220 package=THT]
  R7 = Resistor [tolerance=±5% resistance=220 package=THT]
  R14 = Resistor [tolerance=±5% resistance=10k package=THT]
  + = Antenna
  part = Antenna  # not connected
  10k_B = Rotary Potentiometer (Small) [maximum_resistance=10kΩ]
  C1 = Ceramic Capacitor [capacitance=0.1µF package="200 mil [THT, multilayer]"]
  C2 = Ceramic Capacitor [capacitance=0.1µF package="200 mil [THT, multilayer]"]
  C3 = Ceramic Capacitor [capacitance=0.1µF package="200 mil [THT, multilayer]"]
  C4 = Ceramic Capacitor [capacitance=0.1µF package="200 mil [THT, multilayer]"]
  C5 = Ceramic Capacitor [capacitance=0.1µF package="200 mil [THT, multilayer]"]
  C6 = Ceramic Capacitor [capacitance=0.1µF package="200 mil [THT, multilayer]"]
  C7 = Ceramic Capacitor [capacitance=100nF package="200 mil [THT, multilayer]"]
  100k_A = Rotary Potentiometer (Small) [maximum_resistance=100kΩ]
  R4 = Resistor [tolerance=±5% resistance=220 package=THT]
  PC = Resistor [tolerance=±5% resistance=220 package=THT]
  PC_2 = Resistor [tolerance=±5% resistance=220 package=THT]
  R5 = Resistor [tolerance=±5% resistance=220 package=THT]
  PC_3 = Resistor [tolerance=±5% resistance=220 package=THT]
  R6 = Resistor [tolerance=±5% resistance=220 package=THT]
  PC_4 = Resistor [tolerance=±5% resistance=220 package=THT]
  R2 = Resistor [tolerance=±5% resistance=220 package=THT]
  PC_5 = Resistor [tolerance=±5% resistance=220 package=THT]
  PC_6 = Resistor [tolerance=±5% resistance=220 package=THT]
  R3 = Resistor [tolerance=±5% resistance=220 package=THT]
  40106 = IC, DIP package, 8 pins [chip_label=IC spacing=300mil]
  C8 = Ceramic Capacitor [capacitance=100nF package="200 mil [THT, multilayer]"]
  R1 = Resistor [tolerance=±5% resistance=220 package=THT]

nets:
  N1: darcyneal_com.Pin_1, C6.1, PC.Pin_1
  N2: darcyneal_com.Pin_2, R4.Pin_0
  GND: darcyneal_com.Pin_3, R13.Pin_0, C1.0, C2.0, C3.0, C4.0, C5.0, C6.0, 100k_A.leg1, C8.0
  N3: darcyneal_com.Pin_4, R1.Pin_1
  N4: darcyneal_com.Pin_5, C3.1, PC_4.Pin_0
  N5: darcyneal_com.Pin_6, R2.Pin_1
  N6: R11.Pin_0, R10.Pin_0, R12.Pin_0, C10.+, R9.Pin_0, R8.Pin_0, R7.Pin_0
  N7: R11.Pin_1, R5.Pin_1, PC_3.Pin_0
  N8: R10.Pin_1, R4.Pin_1, PC.Pin_0
  N9: R12.Pin_1, PC_2.Pin_0, R6.Pin_1
  N10: C10.-, R14.Pin_1, C7.0
  N11: C9.-, 100k_A.leg2
  N12: C9.+, 10k_B.wiper
  N13: R13.Pin_1, 10k_B.leg2, C7.1
  N14: R9.Pin_1, PC_6.Pin_1, R3.Pin_0
  N15: R8.Pin_1, R2.Pin_0, PC_5.Pin_1
  N16: R7.Pin_1, PC_4.Pin_1, R1.Pin_0
  N17: R14.Pin_0, 10k_B.leg1, C8.1
  N18: +.antenna_lead, 40106.pin8
  N19: C1.1, PC_6.Pin_0, 40106.pin7
  N20: C2.1, PC_5.Pin_0, 40106.pin5
  N21: C4.1, PC_2.Pin_1, 40106.pin1
  N22: C5.1, PC_3.Pin_1, 40106.pin3
  N23: R5.Pin_0, 40106.pin4
  N24: R6.Pin_0, 40106.pin2
  N25: R3.Pin_1, 40106.pin6

notes:
  All Seeing Eyes
  DarcyNeal.com
