# Fritzing sketch 40106 TerminalStrip Layout (saved by Fritzing 0.9.1b)
circuit board: 7.00059cm x 5.59085cm
breadboards: 1

parts:
  C10 = Electrolytic Capacitor [capacitance=1µF package="100 mil [THT, electrolytic]"]
  C9 = Electrolytic Capacitor [capacitance=1µF package="100 mil [THT, electrolytic]"]
  R13 = Resistor [tolerance=±5% resistance=2.2k package=THT]
  R14 = Resistor [tolerance=±5% resistance=10k package=THT]
  + = Antenna  # not connected
  part = Antenna
  C7 = Ceramic Capacitor [capacitance=100nF package="200 mil [THT, multilayer]"]
  C8 = Ceramic Capacitor [capacitance=100nF package="200 mil [THT, multilayer]"]
  100k_A = Rotary Potentiometer (Small) [maximum_resistance=100kΩ package=THT]
  10k_B = Rotary Potentiometer (Small) [maximum_resistance=10kΩ package=THT]
  J4 = screw terminal, 6 pins  # not connected
  J5 = screw terminal, 6 pins  # not connected
  J6 = female pin header, 3 pins [form="♀ (female)"]
  J7 = female pin header, 3 pins [form="♀ (female)"]
  R15 = Resistor [tolerance=±5% resistance=2.2k package=THT]
  R16 = Resistor [tolerance=±5% resistance=2.2k package=THT]
  R17 = Resistor [tolerance=±5% resistance=2.2k package=THT]
  R18 = Resistor [tolerance=±5% resistance=2.2k package=THT]
  R19 = Resistor [tolerance=±5% resistance=2.2k package=THT]
  R20 = Resistor [tolerance=±5% resistance=2.2k package=THT]
  TRS1 = Audio Jack (TRS) 3.5mm [package="PG203J [THT]"]
  C11 = Ceramic Capacitor [capacitance=100nF package="100 mil [THT, multilayer]"]
  C12 = Ceramic Capacitor [capacitance=100nF package="100 mil [THT, multilayer]"]
  C13 = Ceramic Capacitor [capacitance=100nF package="100 mil [THT, multilayer]"]
  C14 = Ceramic Capacitor [capacitance=100nF package="100 mil [THT, multilayer]"]
  C15 = Ceramic Capacitor [capacitance=100nF package="100 mil [THT, multilayer]"]
  C16 = Ceramic Capacitor [capacitance=100nF package="100 mil [THT, multilayer]"]
  J8 = double row female pin header, 6 pins [form="♀ (female)"]  # not connected

nets:
  N1: C10.-, R14.Pin_1, C7.0
  N2: C10.+, R15.Pin_1, R16.Pin_1, R17.Pin_1, R18.Pin_1, R19.Pin_1, R20.Pin_1
  N3: C9.-, 100k_A.leg2
  N4: C9.+, 10k_B.wiper
  GND: R13.Pin_0, part.antenna_lead, C8.0, 100k_A.leg1, 100k_A.wiper, TRS1.Sleeve, TRS1.Tip
  N5: R13.Pin_1, C7.1, 10k_B.leg2
  N6: R14.Pin_0, C8.1, 10k_B.leg1
  N7: J6.pin1, C11.0
  N8: J6.pin2, C13.0
  N9: J6.pin3, C12.0
  N10: J7.pin1, C14.0
  N11: J7.pin2, C15.0
  N12: J7.pin3, C16.0
  N13: R15.Pin_0, C15.1
  N14: R16.Pin_0, C16.1
  N15: R17.Pin_0, C14.1
  N16: R18.Pin_0, C11.1
  N17: R19.Pin_0, C12.1
  N18: R20.Pin_0, C13.1

notes:
  All Seeing Eyes
